// Logisim project Circuitos Somadores.circ as structural Verilog: 5 circuits, main circuit Meio somador
module Meio_somador (
  input  A,
  input  B,
  output s,
  output Cout
);

  xor xor_1 (s, A, B);
  and and_1 (Cout, A, B);
endmodule

module Somador_Completo__1_bit (
  input  A,
  input  B,
  input  Cin,
  output S,
  output Cout
);

  wire and_1_out, and_2_out, xor_1_out;

  xor xor_1 (xor_1_out, A, B);
  and and_1 (and_1_out, A, B);
  and and_2 (and_2_out, xor_1_out, Cin);
  xor xor_2 (S, xor_1_out, Cin);
  or or_1 (Cout, and_2_out, and_1_out);

  // Notes on the sheet:
  //   VEM
  //   Saida
  //   VAI
endmodule

module Somador_Completo__4_bits (
  input  Cin,
  input  A0,
  input  A1,
  input  A2,
  input  A3,
  input  B0,
  input  B1,
  input  B2,
  input  B3,
  output S0,
  output S1,
  output S2,
  output S3,
  output Cout,
  output Overflow
);

  wire somador_completo_1_bit_1_cout, somador_completo_1_bit_2_cout, somador_completo_1_bit_3_cout;

  Somador_Completo__1_bit somador_completo_1_bit_1 (
    .A(A0), .B(B0), .Cin(Cin), .S(S0), .Cout(somador_completo_1_bit_1_cout));
  Somador_Completo__1_bit somador_completo_1_bit_2 (
    .A(A1), .B(B1), .Cin(somador_completo_1_bit_1_cout), .S(S1), .Cout(somador_completo_1_bit_2_cout));
  Somador_Completo__1_bit somador_completo_1_bit_3 (
    .A(A2), .B(B2), .Cin(somador_completo_1_bit_2_cout), .S(S2), .Cout(somador_completo_1_bit_3_cout));
  Somador_Completo__1_bit somador_completo_1_bit_4 (
    .A(A3), .B(B3), .Cin(somador_completo_1_bit_3_cout), .S(S3), .Cout(Cout));
  xor xor_1 (Overflow, somador_completo_1_bit_3_cout, Cout);
endmodule

module Calculadora_de_4_bits (
  input  A0,
  input  A1,
  input  A2,
  input  Cin,
  input  A3,
  input  B0,
  input  B1,
  input  B2,
  input  B3,
  output S0,
  output S1,
  output S2,
  output S3,
  output Overflow,
  output Cout
);

  wire decodificador_1_a_2, decodificador_1_b_2, decodificador_1_c_2, decodificador_1_d_2, decodificador_1_e,
       decodificador_1_f, decodificador_1_g, decodificador_2_a_2, decodificador_2_b_2, decodificador_2_c_2,
       decodificador_2_d_2, decodificador_2_e, decodificador_2_f, decodificador_2_g, decodificador_3_a_2,
       decodificador_3_b_2, decodificador_3_c_2, decodificador_3_d_2, decodificador_3_e, decodificador_3_f,
       decodificador_3_g;

  Somador_Completo__4_bits somador_completo_4_bits_1 (
    .Cin(Cin), .A0(A0), .A1(A1), .A2(A2), .A3(A3), .B0(B0), .B1(B1), .B2(B2), .B3(B3), .Cout(Cout), .S0(S0),
    .S1(S1), .S2(S2), .S3(S3), .Overflow(Overflow));
  Decodificador decodificador_1 (
    .A(A3), .B(A2), .C(A1), .D(A0), .a_2(decodificador_1_a_2), .b_2(decodificador_1_b_2),
    .c_2(decodificador_1_c_2), .d_2(decodificador_1_d_2), .e(decodificador_1_e), .f(decodificador_1_f),
    .g(decodificador_1_g));
  Decodificador decodificador_2 (
    .A(B3), .B(B2), .C(B1), .D(B0), .a_2(decodificador_2_a_2), .b_2(decodificador_2_b_2),
    .c_2(decodificador_2_c_2), .d_2(decodificador_2_d_2), .e(decodificador_2_e), .f(decodificador_2_f),
    .g(decodificador_2_g));
  _7_Segment_Display u_7_segment_display_1 (
    .g(decodificador_1_g), .f(decodificador_1_f), .a(decodificador_1_a_2), .b(decodificador_1_b_2),
    .e(decodificador_1_e), .d(decodificador_1_d_2), .c(decodificador_1_c_2));  // open: dp
  Decodificador decodificador_3 (
    .A(S3), .B(S2), .C(S1), .D(S0), .a_2(decodificador_3_a_2), .b_2(decodificador_3_b_2),
    .c_2(decodificador_3_c_2), .d_2(decodificador_3_d_2), .e(decodificador_3_e), .f(decodificador_3_f),
    .g(decodificador_3_g));
  _7_Segment_Display u_7_segment_display_2 (
    .g(decodificador_2_g), .f(decodificador_2_f), .a(decodificador_2_a_2), .b(decodificador_2_b_2),
    .e(decodificador_2_e), .d(decodificador_2_d_2), .c(decodificador_2_c_2));  // open: dp
  _7_Segment_Display u_7_segment_display_3 (
    .g(decodificador_3_g), .f(decodificador_3_f), .a(decodificador_3_a_2), .b(decodificador_3_b_2),
    .e(decodificador_3_e), .d(decodificador_3_d_2), .c(decodificador_3_c_2));  // open: dp

  // Notes on the sheet:
  //   Gabriel Henrique Vieira de Oliveira - 775799
endmodule

module Decodificador (
  input  A,
  input  B,
  input  C,
  input  D,
  output a_2,
  output b_2,
  output c_2,
  output d_2,
  output e,
  output f,
  output g
);

  wire and_1_out, and_2_out, and_3_out, and_4_out, and_5_out, and_6_out, and_7_out, and_8_out, and_9_out,
       and_10_out, and_11_out, and_12_out, and_13_out, and_14_out, and_15_out, and_16_out, and_17_out,
       and_18_out, and_19_out, and_20_out, and_21_out, and_22_out, and_23_out, and_24_out, and_25_out,
       and_26_out, and_27_out, and_28_out, and_29_out, and_30_out, and_31_out, and_32_out, not_1_out,
       not_2_out, not_3_out, not_4_out, not_5_out, not_6_out, not_7_out, not_8_out, not_9_out, not_10_out,
       not_11_out, not_12_out, not_13_out, not_14_out, not_15_out, not_16_out, not_17_out, not_18_out,
       not_19_out, not_20_out, not_21_out, not_22_out, not_23_out, not_24_out, not_25_out, not_26_out,
       not_27_out, not_28_out, not_29_out, not_30_out, not_31_out, not_32_out, not_33_out, not_34_out,
       not_35_out, not_36_out, not_37_out, not_38_out, not_39_out, not_40_out, not_41_out, not_42_out;

  not not_1 (not_1_out, B);
  and and_1 (and_1_out, not_1_out, not_2_out);
  not not_2 (not_2_out, D);
  not not_3 (not_3_out, A);
  and and_2 (and_2_out, not_3_out, C);
  not not_4 (not_4_out, A);
  and and_3 (and_3_out, not_4_out, B, D);
  and and_4 (and_4_out, B, C);
  not not_5 (not_5_out, B);
  and and_5 (and_5_out, A, not_5_out, not_6_out);
  not not_6 (not_6_out, C);
  not not_7 (not_7_out, A);
  and and_6 (and_6_out, not_7_out, not_8_out);
  not not_8 (not_8_out, B);
  not not_9 (not_9_out, A);
  and and_7 (and_7_out, not_9_out, not_10_out, not_11_out);
  not not_10 (not_10_out, C);
  not not_11 (not_11_out, D);
  not not_12 (not_12_out, B);
  and and_8 (and_8_out, not_12_out, not_13_out);
  not not_13 (not_13_out, D);
  not not_14 (not_14_out, A);
  and and_9 (and_9_out, not_14_out, C, D);
  not not_15 (not_15_out, C);
  and and_10 (and_10_out, A, not_15_out, D);
  not not_16 (not_16_out, A);
  and and_11 (and_11_out, not_16_out, not_17_out);
  not not_17 (not_17_out, C);
  not not_18 (not_18_out, A);
  and and_12 (and_12_out, not_18_out, D);
  not not_19 (not_19_out, C);
  and and_13 (and_13_out, not_19_out, D);
  not not_20 (not_20_out, A);
  and and_14 (and_14_out, not_20_out, B);
  and and_15 (and_15_out, A, not_21_out);
  not not_21 (not_21_out, B);
  not not_22 (not_22_out, A);
  and and_16 (and_16_out, not_22_out, not_23_out, not_24_out);
  not not_23 (not_23_out, B);
  not not_24 (not_24_out, D);
  not not_25 (not_25_out, B);
  and and_17 (and_17_out, not_25_out, C, D);
  not not_26 (not_26_out, C);
  and and_18 (and_18_out, B, not_26_out, D);
  and and_19 (and_19_out, B, C, not_27_out);
  not not_27 (not_27_out, D);
  and and_20 (and_20_out, A, not_28_out);
  not not_28 (not_28_out, C);
  not not_29 (not_29_out, B);
  and and_21 (and_21_out, not_29_out, not_30_out);
  not not_30 (not_30_out, D);
  and and_22 (and_22_out, C, not_31_out);
  not not_31 (not_31_out, D);
  and and_23 (and_23_out, A, C);
  and and_24 (and_24_out, A, B);
  not not_32 (not_32_out, A);
  and and_25 (and_25_out, not_32_out, not_33_out, not_34_out);
  not not_33 (not_33_out, C);
  not not_34 (not_34_out, D);
  not not_35 (not_35_out, A);
  and and_26 (and_26_out, not_35_out, B, not_36_out);
  not not_36 (not_36_out, C);
  not not_37 (not_37_out, A);
  and and_27 (and_27_out, not_37_out, B, not_38_out);
  not not_38 (not_38_out, D);
  and and_28 (and_28_out, A, not_39_out);
  not not_39 (not_39_out, B);
  and and_29 (and_29_out, A, C);
  not not_40 (not_40_out, B);
  and and_30 (and_30_out, not_40_out, C);
  and and_31 (and_31_out, B, not_41_out);
  not not_41 (not_41_out, C);
  and and_32 (and_32_out, B, not_42_out);
  not not_42 (not_42_out, D);
  or or_1 (a_2, and_1_out, and_2_out, and_3_out, and_4_out, and_5_out);
  or or_2 (b_2, and_6_out, and_7_out, and_8_out, and_9_out, and_10_out);
  or or_3 (c_2, and_11_out, and_12_out, and_13_out, and_14_out, and_15_out);
  or or_4 (d_2, and_16_out, and_17_out, and_18_out, and_19_out, and_20_out);
  or or_5 (e, and_21_out, and_22_out, and_23_out, and_24_out);
  or or_6 (f, and_25_out, and_26_out, and_27_out, and_28_out, and_29_out);
  or or_7 (g, and_30_out, and_31_out, and_32_out, A);
  _7_Segment_Display u_7_segment_display_1 (.g(g), .f(f), .a(a_2), .b(b_2), .e(e), .d(d_2), .c(c_2));  // open: dp
endmodule
