// Logisim project ULAs.circ as structural Verilog: 5 circuits, main circuit MUX da ULA
module MUX_da_ULA (
  input  m,
  input  n,
  input  o,
  input  p,
  input  OP1,
  input  OP0,
  output out_7
);

  wire and_1_out, and_2_out, and_3_out, and_4_out, not_1_out, not_2_out, not_3_out, not_4_out;

  not not_1 (not_1_out, OP1);
  not not_2 (not_2_out, OP0);
  not not_3 (not_3_out, OP1);
  not not_4 (not_4_out, OP0);
  and and_1 (and_1_out, m, not_1_out, not_2_out);
  and and_2 (and_2_out, n, not_3_out, OP0);
  and and_3 (and_3_out, o, OP1, not_4_out);
  and and_4 (and_4_out, p, OP1, OP0);
  or or_1 (out_7, and_1_out, and_2_out, and_3_out, and_4_out);
endmodule

module MUXINHO_Binvert (
  input  Sel,
  input  A,
  input  B,
  output F
);

  wire and_1_out, and_2_out, not_1_out;

  not not_1 (not_1_out, Sel);
  and and_1 (and_1_out, A, not_1_out);
  and and_2 (and_2_out, Sel, B);
  or or_1 (F, and_1_out, and_2_out);
endmodule

module ULA_de_1bit (
  input  Binvert,
  input  Cin,
  input  A,
  input  OP1,
  input  OP0,
  input  B,
  output F,
  output Cout
);

  wire and_1_out, muxinho_binvert_1_f, not_1_out, not_2_out, or_1_out, somador_1bit_1_s;

  not not_1 (not_1_out, B);
  MUXINHO_Binvert muxinho_binvert_1 (.A(B), .B(not_1_out), .Sel(Binvert), .F(muxinho_binvert_1_f));
  and and_1 (and_1_out, A, muxinho_binvert_1_f);
  or or_1 (or_1_out, A, muxinho_binvert_1_f);
  not not_2 (not_2_out, A);
  Somador_1bit somador_1bit_1 (.A(A), .B(muxinho_binvert_1_f), .Cin(Cin), .S(somador_1bit_1_s), .Cout(Cout));
  MUX_da_ULA mux_da_ula_1 (
    .m(and_1_out), .n(or_1_out), .o(not_2_out), .p(somador_1bit_1_s), .OP1(OP1), .OP0(OP0), .out_7(F));
endmodule

module Somador_1bit (
  input  A,
  input  B,
  input  Cin,
  output S,
  output Cout
);

  wire and_1_out, and_2_out, xor_1_out;

  xor xor_1 (xor_1_out, A, B);
  and and_1 (and_1_out, A, B);
  and and_2 (and_2_out, xor_1_out, Cin);
  xor xor_2 (S, xor_1_out, Cin);
  or or_1 (Cout, and_2_out, and_1_out);

  // Notes on the sheet:
  //   VEM
  //   Saida
  //   VAI
endmodule

module ULA_de_4bits (
  input  Binvert,
  input  B3,
  input  B2,
  input  B1,
  input  B0,
  input  A3,
  input  A2,
  input  A1,
  input  A0,
  input  OP1,
  input  OP0,
  output S3,
  output S2,
  output S1,
  output S0,
  output Cout
);

  wire ula_de_1bit_1_cout, ula_de_1bit_2_cout, ula_de_1bit_3_cout;

  ULA_de_1bit ula_de_1bit_1 (
    .A(A0), .B(B0), .Binvert(Binvert), .Cin(Binvert), .OP1(OP1), .OP0(OP0), .F(S0), .Cout(ula_de_1bit_1_cout));
  ULA_de_1bit ula_de_1bit_2 (
    .A(A1), .B(B1), .Binvert(Binvert), .Cin(ula_de_1bit_1_cout), .OP1(OP1), .OP0(OP0), .F(S1),
    .Cout(ula_de_1bit_2_cout));
  ULA_de_1bit ula_de_1bit_3 (
    .A(A2), .B(B2), .Binvert(Binvert), .Cin(ula_de_1bit_2_cout), .OP1(OP1), .OP0(OP0), .F(S2),
    .Cout(ula_de_1bit_3_cout));
  ULA_de_1bit ula_de_1bit_4 (
    .A(A3), .B(B3), .Binvert(Binvert), .Cin(ula_de_1bit_3_cout), .OP1(OP1), .OP0(OP0), .F(S3), .Cout(Cout));

  // Notes on the sheet:
  //   Cin
endmodule
